# Fritzing sketch NapkinFire (saved by Fritzing 0.9.3b)
circuit board: 6.25cm x 6.25cm
breadboards: 1

parts:
  Part1 = Adafruit HUZZAH32 ESP32 Feather [part_number="Adafruit #3405"]
  SG1 = Buzzer 12mm [package=buzzer-12mm-ns]
  J65 = Piezo Speaker
  PIR1 = PIR sensor
  J67 = double row female pin header, 16 pins [form="♀ (female)"]
  J68 = double row female pin header, 16 pins [form="♀ (female)"]
  J69 = double row female pin header, 16 pins [form="♀ (female)"]
  J70 = double row female pin header, 16 pins [form="♀ (female)"]
  CAM1 = Arducam [package=THT]
  R1 = Resistor [tolerance=±5% resistance=220 package="0805 [SMD]"]

nets:
  GND: Part1.IO21, Part1.IO17, Part1.IO16, Part1.GND, SG1.1, J65.pin1, PIR1.GND, J67.pin1, J67.pin2, J67.pin3, J67.pin4, J67.pin5, J67.pin6, J67.pin7, J67.pin8, J67.pin9, J67.pin10, J67.pin11, J67.pin12, J67.pin13, J67.pin14, J67.pin15, J67.pin16, J68.pin1, J68.pin2, J68.pin3, J68.pin4, J68.pin5, J68.pin6, J68.pin7, J68.pin8, J68.pin9, J68.pin10, J68.pin11, J68.pin12, J68.pin13, J68.pin14, J68.pin15, J68.pin16, J69.pin1, J69.pin2, J69.pin3, J69.pin4, J69.pin5, J69.pin6, J69.pin7, J69.pin8, J69.pin9, J69.pin10, J69.pin11, J69.pin12, J69.pin13, J69.pin14, J69.pin15, J69.pin16, J70.pin1, J70.pin2, J70.pin3, J70.pin4, J70.pin5, J70.pin6, J70.pin7, J70.pin8, J70.pin9, J70.pin10, J70.pin11, J70.pin12, J70.pin13, J70.pin14, J70.pin15, J70.pin16, CAM1.GND, R1.Pin_1
  N1: Part1.MISO, CAM1.MISO
  N2: Part1.MOSI, CAM1.MOSI
  N3: Part1.SCK, CAM1.SCK
  3.3V: Part1.3.3V, PIR1.VDD, CAM1.VCC, R1.Pin_0
  N4: Part1.IO27_A10, PIR1.SIG
  N5: Part1.IO15_A8, SG1.2
  N6: Part1.IO32_A7, J65.pin2
  N7: Part1.IO14_A6, CAM1.CS
  N8: Part1.SCL, CAM1.SCL
  N9: Part1.SDA, CAM1.SDA

notes:
  3V
  0V
  IO1
  IO2
  IO3

custom parts:
  Arducam: A Arducam moudle
